# Fritzing sketch 11.Encender_un_led_while_otro_apa (saved by Fritzing 0.9.6b)
breadboards: 1

parts:
  Componente1 = Arduino Uno (Rev3)
  LED1 = LED - 5mm [color="Red (633nm)" current=0.030 package="5 mm [THT]"]
  LED2 = LED - 5mm [color="Blue (525nm)" current=0.030 package="5 mm [THT]"]

nets:
  N1: Componente1.D10_PWM/SS, LED2.anode
  N2: Componente1.D13/SCK, LED1.anode
  N3: Componente1.GND, LED1.cathode, LED2.cathode
