# Fritzing sketch 14.Encender_1_de_3_leds (saved by Fritzing 0.9.6b)
breadboards: 1

parts:
  Componente1 = Arduino Uno (Rev3)
  LED1 = LED - 5mm [color="Red (633nm)" current=0.030 package="5 mm [THT]"]
  LED2 = LED - 5mm [color="Blue (525nm)" current=0.030 package="5 mm [THT]"]
  LED3 = LED - 5mm [color="White (4500K)" current=0.030 package="5 mm [THT]"]

nets:
  N1: Componente1.D8, LED3.anode
  N2: Componente1.D10_PWM/SS, LED2.anode
  N3: Componente1.D13/SCK, LED1.anode
  N4: Componente1.GND, LED1.cathode, LED2.cathode, LED3.cathode
