# Fritzing sketch 2.BotonLed (saved by Fritzing 0.9.6b)
breadboards: 1

parts:
  Componente1 = Arduino Uno (Rev3)
  LED1 = LED - 5mm [color="Red (633nm)" current=0.030 package="5 mm [THT]"]
  S1 = Pushbutton [package="[SMD]"]

nets:
  N1: Componente1.D13/SCK, LED1.anode
  N2: Componente1.GND, LED1.cathode, S1.Pin_1, S1.Pin_2
  N3: Componente1.D7, S1.Pin_3, S1.Pin_4
