# Fritzing sketch 4.Ultrasonico (saved by Fritzing 0.9.6b)
breadboards: 1

parts:
  Componente1 = Arduino Uno (Rev3)
  HC-SR04_Sensor_1 = HC-SR04 Ultrasonic Distance Sensor

nets:
  N1: Componente1.D4, HC-SR04_Sensor_1.ECHO
  N2: Componente1.D5_PWM, HC-SR04_Sensor_1.TRIG
  5V: Componente1.5V, HC-SR04_Sensor_1.VCC
  GND: Componente1.GND, HC-SR04_Sensor_1.GND
