# Fritzing sketch 6.fotosensor (saved by Fritzing 0.9.6b)
breadboards: 1

parts:
  Componente1 = Arduino Uno (Rev3)
  LED1 = LED - 3mm [color="Red (633nm)" current=0.030 package="3 mm [THT]"]
  R1 = Photocell (LDR) [package=THT]

nets:
  N1: Componente1.A0, R1.pin_0
  N2: Componente1.D13/SCK, LED1.anode
  N3: Componente1.5V, R1.pin_1
  N4: Componente1.GND, LED1.cathode
