# Fritzing sketch Esp32 (saved by Fritzing 0.9.6b)
breadboards: 1

parts:
  LED1 = smd LED [color="Red (633nm)" package="1206 [SMD]"]
  R1 = Resistor [tolerance=±5% resistance=220 package="2512 [SMD]"]
  U1 = ESP32-38PinWide [part_number=ESP32-38PinWide]
  DHT2 = DHT11 Humitidy and Temperature Sensor

nets:
  VIN: LED1.cathode, U1.VIN, DHT2.VDD
  N1: LED1.anode, R1.Pin_0
  N2: U1.3.3, DHT2.GND
  N3: U1.GPIO15, DHT2.DATA

custom parts:
  ESP32-38PinWide: Generic 38-Pin ESP32 with wide format (only access to one side of pins on a breadboard) based on Stephen Lilley's HiLetgo ESP-WROOM-32 ESP32 ESP-32S Development Board.
  DHT11 Humitidy and Temperature Sensor: DHT11 Humidity and Temperature Sensor
