# Fritzing sketch Plantilla Arduino Uno (saved by Fritzing 0.9.6b)
breadboards: 1

parts:
  Componente1 = Arduino Uno (Rev3)
  Part3 = Bluetooth HC-05 Macho
  LED1 = smd LED [color="Red (633nm)" package="1206 [SMD]"]
  R1 = Resistor [tolerance=±5% resistance=220 package="2512 [SMD]"]

nets:
  N1: Componente1.D10_PWM/SS, Part3.TXD
  N2: Componente1.D11_PWM/MOSI, Part3.RXD
  N3: Componente1.D13/SCK, R1.Pin_1
  5V: Componente1.5V, Part3.VCC
  GND: Componente1.GND, Part3.GND, LED1.cathode
  N4: LED1.anode, R1.Pin_0
